// Logisim project PSD-01.circ as structural Verilog: 1 circuit, main circuit main
module main (
  input  D,
  input  A,
  input  [2:0] BCD,
  input  [2:0] ABC
);

  wire decoder_1_out0, decoder_1_out1, decoder_1_out2, decoder_1_out3, decoder_1_out4, decoder_1_out5,
       decoder_1_out6, decoder_1_out7, decoder_2_out0, decoder_2_out1, decoder_2_out2, decoder_2_out3,
       decoder_2_out4, decoder_2_out5, decoder_2_out6, decoder_2_out7, multiplexer_1_out, not_1_out, or_1_out;

  Multiplexer #(.select(3), .enable("false")) multiplexer_1 (
    .in0(1'b1), .in1(D), .in2(D), .in3(1'b0), .in4(1'b1), .in5(1'b0), .in6(1'b0), .in7(1'b1),
    .out(multiplexer_1_out), .sel(ABC));
  LED led_1 (.in(multiplexer_1_out));
  not not_1 (not_1_out, A);
  Decoder #(.select(3)) decoder_1 (
    .out0(decoder_1_out0), .out1(decoder_1_out1), .out2(decoder_1_out2), .out3(decoder_1_out3),
    .out4(decoder_1_out4), .out5(decoder_1_out5), .out6(decoder_1_out6), .out7(decoder_1_out7), .sel(BCD),
    .en(not_1_out));
  Decoder #(.select(3)) decoder_2 (
    .out0(decoder_2_out0), .out1(decoder_2_out1), .out2(decoder_2_out2), .out3(decoder_2_out3),
    .out4(decoder_2_out4), .out5(decoder_2_out5), .out6(decoder_2_out6), .out7(decoder_2_out7), .sel(BCD),
    .en(A));
  or or_1 (or_1_out, decoder_1_out0, decoder_1_out1, decoder_1_out3, decoder_1_out5, decoder_2_out0, decoder_2_out1, decoder_2_out6, decoder_2_out7);
  LED led_2 (.in(or_1_out));

  // Notes on the sheet:
  //   GND
  //   i0
  //   i2
  //   i3
  //   i1
  //   i4
  //   i5
  //   i7
  //   i6
  //   i9
  //   i8
  //   i14
  //   i11
  //   i15
  //   i12
  //   i10
  //   i13
endmodule
