// Logisim project PSD-02.circ as structural Verilog: 1 circuit, main circuit main
module main (
  input  C,
  input  [2:0] ABC,
  input  [1:0] AB,
  output SUM,
  output CARRY,
  output SUM_2,
  output CARRY_2
);

  wire decoder_1_out0, decoder_1_out1, decoder_1_out2, decoder_1_out3, decoder_1_out4, decoder_1_out5,
       decoder_1_out6, decoder_1_out7, not_1_out;

  not not_1 (not_1_out, C);
  Multiplexer #(.select(2), .enable("false")) multiplexer_1 (
    .in0(C), .in1(not_1_out), .in2(not_1_out), .in3(C), .out(SUM), .sel(AB));
  Multiplexer #(.select(2), .enable("false")) multiplexer_2 (
    .in0(1'b0), .in1(C), .in2(C), .in3(1'b0), .out(CARRY), .sel(AB));
  Decoder #(.select(3), .enable("false")) decoder_1 (
    .out0(decoder_1_out0), .out1(decoder_1_out1), .out2(decoder_1_out2), .out3(decoder_1_out3),
    .out4(decoder_1_out4), .out5(decoder_1_out5), .out6(decoder_1_out6), .out7(decoder_1_out7), .sel(ABC));
  or or_1 (SUM_2, decoder_1_out1, decoder_1_out2, decoder_1_out4, decoder_1_out7);
  or or_2 (CARRY_2, decoder_1_out3, decoder_1_out5, decoder_1_out6, decoder_1_out7);
endmodule
