// Logisim project PSD-03.circ as structural Verilog: 1 circuit, main circuit main
module main (
  input  C,
  input  A,
  input  B
);

  wire and_1_out, and_2_out, and_3_out, and_4_out, not_1_out, not_2_out, or_1_out, or_2_out, or_3_out;

  not not_1 (not_1_out, A);
  not not_2 (not_2_out, B);
  and and_1 (and_1_out, 1'b1, not_1_out, not_2_out);
  and and_2 (and_2_out, 1'b0, not_1_out, B);
  and and_3 (and_3_out, C, A, not_2_out);
  and and_4 (and_4_out, C, A, B);
  or or_1 (or_1_out, and_1_out, and_2_out);
  or or_2 (or_2_out, or_1_out, or_3_out);
  or or_3 (or_3_out, and_3_out, and_4_out);
  LED led_1 (.in(or_2_out));

  // Notes on the sheet:
  //   GND
  //   S2
  //   S1
endmodule
